# Fritzing sketch Sketch (saved by Fritzing 0.9.3b)
circuit board: 4.38962cm x 5.57475cm
breadboards: 1

parts:
  Gizwits_WiFi_Witty_ESP-12F1 = Gizwits WiFi Witty ESP-12F
  RHT1 = Humidity and Temperature Sensor RHT03
  J1 = Screw terminal - 2 pins [package=THT]

nets:
  N1: Gizwits_WiFi_Witty_ESP-12F1.REST, Gizwits_WiFi_Witty_ESP-12F1.GPIO16
  VCC: Gizwits_WiFi_Witty_ESP-12F1.VCC, RHT1.Vcc, J1.pin1
  N2: Gizwits_WiFi_Witty_ESP-12F1.GND, RHT1.GND_1, RHT1.GND_2, J1.pin2
  N3: Gizwits_WiFi_Witty_ESP-12F1.GPIO4, RHT1.Data-signal

notes:
  HD Weather Station
