# Fritzing sketch Sketch2 (saved by Fritzing 0.9.3b)
breadboards: 1

parts:
  U1 = ESP8266 WiFi Module [part_number=ESP8266]
  VCC1 = Battery block 9V
  Q1 = NPN-Transistor [package="TO92 [THT]"]
  U2 = RELAY [package=relay-jzc]

nets:
  N1: U1.VCC, U1.CH_PD
  N2: U1.GND, VCC1.-
  N3: U1.GPIO_5, Q1.B
  N4: U1.GPIO_16, U1.REST
  N5: VCC1.+, U2.MAIN
  N6: Q1.C, U2.COIL1
